# Fritzing sketch HX1838 (saved by Fritzing 0.9.2b)

parts:
  Raspberry_Pi1 = Raspberry Pi B+
  LED1 = DUO LED RG [package="5 mm [THT]"]

nets:
  N1: Raspberry_Pi1.GPIO14, LED1.red_anode
  N2: Raspberry_Pi1.GND, LED1.common_cathode
  N3: Raspberry_Pi1.5V, LED1.green_anode

notes:
  OUT GND VCC
